// Digital circuit solucao.dig as structural Verilog
module solucao (
  input  INTD,
  input  INTC,
  input  INTB,
  input  INTA,
  input  M,
  input  SA,
  input  SB,
  input  SC,
  input  SD,
  output Y
);

  wire and_1_out, and_2_out, multiplexer_1_out;
  wire [1:0] priorityencoder_1_num;

  Multiplexer #(.Selector_Bits(2)) multiplexer_1 (
    .sel(priorityencoder_1_num), .in_0(INTA), .in_1(INTB), .in_2(INTC), .in_3(INTD), .out(multiplexer_1_out));
  PriorityEncoder #(.Selector_Bits(2)) priorityencoder_1 (
    .in0(SA), .in1(SB), .in2(SC), .in3(SD), .num(priorityencoder_1_num));  // open: any
  and and_1 (and_1_out, M, multiplexer_1_out);
  and and_2 (and_2_out, ~M, INTA);  // And
  or or_1 (Y, and_1_out, and_2_out);
endmodule
