// Digital circuit test1.dig as structural Verilog
module test1 (
  input  in_1,
  input  in_3,
  input  in_4,
  input  in_5,
  output out_2,
  output out_6
);

  wire and_1_out, and_2_out, not_1_out, not_2_out, not_3_out;

  not not_1 (not_1_out, in_4);
  not not_2 (not_2_out, in_5);
  and and_1 (and_1_out, in_3, not_1_out, not_2_out);
  and and_2 (and_2_out, in_4, not_3_out);
  not not_3 (not_3_out, in_5);
  or or_1 (out_2, in_5, and_1_out);
  or or_2 (out_6, and_2_out, in_5);
endmodule
