// Digital circuit test2.dig as structural Verilog
module test2 (
  input  in_1,
  input  in_2,
  input  in_3,
  input  in_4,
  input  in_5,
  input  in_6,
  output out_7
);

  wire multiplexer_1_out, multiplexer_2_out;

  Multiplexer multiplexer_1 (.sel(in_5), .in_0(in_1), .in_1(in_2), .out(multiplexer_1_out));
  Multiplexer multiplexer_2 (.sel(in_5), .in_0(in_3), .in_1(in_4), .out(multiplexer_2_out));
  Multiplexer multiplexer_3 (.sel(in_6), .in_0(multiplexer_1_out), .in_1(multiplexer_2_out), .out(out_7));
endmodule
