// Digital circuit Circuitotoplevel.dig as structural Verilog
module Circuitotoplevel (
  input  D,
  input  C,
  output Qld,
  output Qfd,
  output Qft
);

  LATCHD latchd_1 (.D(D), .e(C), .Q(Qld));
  FLIPFLOPD flipflopd_1 (.gt(C), .D(D), .Q(Qfd));
  FLIPFLOPT flipflopt_1 (.T(D), .gt(C), .Q(Qft));
endmodule
