// Digital circuit FLIPFLOPD.dig as structural Verilog
module FLIPFLOPD (
  input  gt,
  input  D,
  output Q
);

  wire latchd_1_q, not_1_out, not_2_out;

  not not_1 (not_1_out, gt);
  LATCHD latchd_1 (.D(D), .e(not_1_out), .Q(latchd_1_q));
  not not_2 (not_2_out, not_1_out);
  LATCHD latchd_2 (.D(latchd_1_q), .e(not_2_out), .Q(Q));
endmodule
