// Digital circuit FLIPFLOPT.dig as structural Verilog
module FLIPFLOPT (
  input  T,
  input  gt,
  output Q
);

  wire multiplexer_1_out, not_1_out;

  Multiplexer multiplexer_1 (.sel(T), .in_0(Q), .in_1(not_1_out), .out(multiplexer_1_out));
  not not_1 (not_1_out, Q);
  FLIPFLOPD flipflopd_1 (.gt(gt), .D(multiplexer_1_out), .Q(Q));
endmodule
