// Digital circuit LATCHD.dig as structural Verilog
module LATCHD (
  input  D,
  input  e,
  output Q
);

  wire nand_1_out, nand_2_out, nand_4_out, not_1_out;

  not not_1 (not_1_out, D);
  nand nand_1 (nand_1_out, D, e);
  nand nand_2 (nand_2_out, not_1_out, e);
  nand nand_3 (Q, nand_1_out, nand_4_out);
  nand nand_4 (nand_4_out, Q, nand_2_out);
endmodule
