// Digital circuit complete.dig as structural Verilog
module complete (
  input  Q,
  input  C,
  output Q_d,
  output Qfd,
  output Qft
);

  latch_d latch_d_1 (.D(Q), .e(C), .Q(Q_d));
  flip_flop_D flip_flop_d_1 (.D(Q), .C(C), .Q(Qfd));
  flip_flop_T flip_flop_t_1 (.T(Q), .C(C), .Q(Qft));
endmodule
