// Digital circuit flip_flop_D.dig as structural Verilog
module flip_flop_D (
  input  D,
  input  C,
  output Q
);

  wire latch_d_1_q, not_1_out, not_2_out;

  not not_1 (not_1_out, C);
  latch_d latch_d_1 (.D(D), .e(not_1_out), .Q(latch_d_1_q));
  not not_2 (not_2_out, not_1_out);
  latch_d latch_d_2 (.D(latch_d_1_q), .e(not_2_out), .Q(Q));
endmodule
