// Digital circuit flip_flop_T.dig as structural Verilog
module flip_flop_T (
  input  T,
  input  C,
  output Q
);

  wire multiplexer_1_out, not_1_out;

  Multiplexer multiplexer_1 (.sel(T), .in_0(Q), .in_1(not_1_out), .out(multiplexer_1_out));
  flip_flop_D flip_flop_d_1 (.D(multiplexer_1_out), .C(C), .Q(Q));
  not not_1 (not_1_out, Q);
endmodule
