// Digital circuit Completo.dig as structural Verilog
module Completo (
  input  D,
  input  C,
  output Qld,
  output Qfd,
  output Qft
);

  Ltd ltd_1 (.D(D), .C(C), .Qld(Qld));
  FLd fld_1 (.D(D), .C(C), .Qfd(Qfd));
  Flt flt_1 (.T(D), .C(C), .Qft(Qft));
endmodule
