// Digital circuit FLd.dig as structural Verilog
module FLd (
  input  D,
  input  C,
  output Qfd
);

  wire ltd_1_qld, not_1_out, not_2_out;

  not not_1 (not_1_out, C);
  Ltd ltd_1 (.D(D), .C(not_1_out), .Qld(ltd_1_qld));
  not not_2 (not_2_out, not_1_out);
  Ltd ltd_2 (.D(ltd_1_qld), .C(not_2_out), .Qld(Qfd));
endmodule
