// Digital circuit Flt.dig as structural Verilog
module Flt (
  input  T,
  input  C,
  output Qft
);

  wire multiplexer_1_out, not_1_out;

  not not_1 (not_1_out, Qft);
  Multiplexer multiplexer_1 (.sel(T), .in_0(Qft), .in_1(not_1_out), .out(multiplexer_1_out));
  FLd fld_1 (.D(multiplexer_1_out), .C(C), .Qfd(Qft));
endmodule
