// Digital circuit Ltd.dig as structural Verilog
module Ltd (
  input  D,
  input  C,
  output Qld
);

  wire nand_1_out, nand_2_out, nand_4_out, not_1_out;

  not not_1 (not_1_out, D);
  nand nand_1 (nand_1_out, D, C);
  nand nand_2 (nand_2_out, C, not_1_out);
  nand nand_3 (Qld, nand_1_out, nand_4_out);
  nand nand_4 (nand_4_out, Qld, nand_2_out);
endmodule
