// Digital circuit Cicruito latch e flip flop.dig as structural Verilog
module Cicruito_latch_e_flip_flop (
  input  D,
  input  C,
  output Qld,
  output Qfd,
  output Qft
);

  Latch_D latch_d_1 (.D(D), .E(C), .Q_d(Qld));
  FlipFlop_D flipflop_d_1 (.D(D), .C(C), .Qfd(Qfd));
  FlipFlop_T flipflop_t_1 (.T(D), .C(C), .Qft(Qft));
endmodule
