// Digital circuit FlipFlop D.dig as structural Verilog
module FlipFlop_D (
  input  D,
  input  C,
  output Qfd
);

  wire latch_d_1_q_d, not_1_out, not_2_out;

  not not_1 (not_1_out, C);
  Latch_D latch_d_1 (.D(D), .E(not_1_out), .Q_d(latch_d_1_q_d));
  not not_2 (not_2_out, not_1_out);
  Latch_D latch_d_2 (.D(latch_d_1_q_d), .E(not_2_out), .Q_d(Qfd));
endmodule
