// Digital circuit FlipFlop T.dig as structural Verilog
module FlipFlop_T (
  input  T,
  input  C,
  output Qft
);

  wire multiplexer_1_out, not_1_out;

  Multiplexer multiplexer_1 (.sel(T), .in_0(Qft), .in_1(not_1_out), .out(multiplexer_1_out));
  FlipFlop_D flipflop_d_1 (.D(multiplexer_1_out), .C(C), .Qfd(Qft));
  not not_1 (not_1_out, Qft);
endmodule
