// Digital circuit Latch D.dig as structural Verilog
module Latch_D (
  input  D,
  input  E,
  output Q_d
);

  wire nand_1_out, nand_2_out, nand_4_out, not_1_out;

  not not_1 (not_1_out, D);
  nand nand_1 (nand_1_out, E, D);
  nand nand_2 (nand_2_out, E, not_1_out);
  nand nand_3 (Q_d, nand_1_out, nand_4_out);
  nand nand_4 (nand_4_out, Q_d, nand_2_out);
endmodule
