// Digital circuit T-flip-flop.dig as structural Verilog
module T_flip_flop (
  input  T,
  input  C,
  output Q,
  output nQ
);

  wire multiplexer_1_out;

  Multiplexer multiplexer_1 (.sel(T), .in_0(Q), .in_1(nQ), .out(multiplexer_1_out));
  D_flip_flop d_flip_flop_1 (.D(multiplexer_1_out), .C(C), .Q(Q), .nQ(nQ));
endmodule
