// Digital circuit contador-up-down.dig as structural Verilog
module contador_up_down (
  input  Enable,
  input  up,
  input  Clk,
  output [3:0] Q
);

  wire multiplexer_1_out, multiplexer_2_out, multiplexer_3_out, t_flip_flop_1_nq, t_flip_flop_2_nq,
       t_flip_flop_3_nq;

  T_flip_flop t_flip_flop_1 (.T(Enable), .C(Clk), .Q(Q[0]), .nQ(t_flip_flop_1_nq));
  Multiplexer multiplexer_1 (.sel(up), .in_0(Q[0]), .in_1(t_flip_flop_1_nq), .out(multiplexer_1_out));
  T_flip_flop t_flip_flop_2 (.T(Enable), .C(multiplexer_1_out), .Q(Q[1]), .nQ(t_flip_flop_2_nq));
  Multiplexer multiplexer_2 (.sel(up), .in_0(Q[1]), .in_1(t_flip_flop_2_nq), .out(multiplexer_2_out));
  T_flip_flop t_flip_flop_3 (.T(Enable), .C(multiplexer_2_out), .Q(Q[2]), .nQ(t_flip_flop_3_nq));
  Multiplexer multiplexer_3 (.sel(up), .in_0(Q[2]), .in_1(t_flip_flop_3_nq), .out(multiplexer_3_out));
  T_flip_flop t_flip_flop_4 (.T(Enable), .C(multiplexer_3_out), .Q(Q[3]));  // open: nQ
endmodule
