// Digital circuit D-flip-flop.dig as structural Verilog
module D_flip_flop (
  input  D,
  input  C,
  output Q
);

  wire d_latch_1_q, not_1_out, not_2_out;

  not not_1 (not_1_out, C);
  D_latch d_latch_1 (.D(D), .e(not_1_out), .Q(d_latch_1_q));
  not not_2 (not_2_out, not_1_out);
  D_latch d_latch_2 (.D(d_latch_1_q), .e(not_2_out), .Q(Q));
endmodule
