// Digital circuit T-flip-flop.dig as structural Verilog
module T_flip_flop (
  input  T,
  input  C,
  output Q
);

  wire multiplexer_1_out, not_1_out;

  not not_1 (not_1_out, Q);
  Multiplexer multiplexer_1 (.sel(T), .in_0(Q), .in_1(not_1_out), .out(multiplexer_1_out));
  D_flip_flop d_flip_flop_1 (.D(multiplexer_1_out), .C(C), .Q(Q));
endmodule
