// Digital circuit circuito-top-level.dig as structural Verilog
module circuito_top_level (
  input  D,
  input  C,
  output Qld,
  output Qfd,
  output Qft
);

  D_latch d_latch_1 (.D(D), .e(C), .Q(Qld));
  D_flip_flop d_flip_flop_1 (.D(D), .C(C), .Q(Qfd));
  T_flip_flop t_flip_flop_1 (.T(D), .C(C), .Q(Qft));
endmodule
