// Digital circuit registrador.dig as structural Verilog
module registrador (
  input  load,
  input  shift,
  input  esquerda,
  input  ep3,
  input  es,
  input  Clk,
  input  ep2,
  output out_8,
  output out_9
);

  wire multiplexer_1_out, multiplexer_2_out, multiplexer_3_out, multiplexer_4_out, multiplexer_5_out,
       multiplexer_6_out;

  Multiplexer multiplexer_1 (.sel(esquerda), .in_0(es), .in_1(out_9), .out(multiplexer_1_out));
  Multiplexer multiplexer_2 (.sel(shift), .in_0(ep3), .in_1(multiplexer_1_out), .out(multiplexer_2_out));
  Multiplexer multiplexer_3 (.sel(load), .in_0(out_8), .in_1(multiplexer_2_out), .out(multiplexer_3_out));
  D_flip_flop d_flip_flop_1 (.D(multiplexer_3_out), .C(Clk), .Q(out_8));
  Multiplexer multiplexer_4 (.sel(esquerda), .in_0(out_8), .in_1(1'b0), .out(multiplexer_4_out));
  Multiplexer multiplexer_5 (.sel(shift), .in_0(ep2), .in_1(multiplexer_4_out), .out(multiplexer_5_out));
  Multiplexer multiplexer_6 (.sel(load), .in_0(out_9), .in_1(multiplexer_5_out), .out(multiplexer_6_out));
  D_flip_flop d_flip_flop_2 (.D(multiplexer_6_out), .C(Clk), .Q(out_9));
endmodule
